# Fritzing sketch esp32-button-photocell (saved by Fritzing 0.9.4)
breadboards: 1

parts:
  Part1 = Adafruit HUZZAH32 ESP32 Feather [part_number="Adafruit #3405"]
  S1 = Momentary Switch [package=ksa_sealed_tac_switch]
  R1 = Photocell (LDR) [package=THT]
  R2 = Resistor [tolerance=±5% resistance=10k package="0805 [SMD]"]
  R3 = Resistor [tolerance=±5% resistance=10k package="0805 [SMD]"]
  R4 = Resistor [tolerance=±5% resistance=1k package="0805 [SMD]"]

nets:
  N1: Part1.SCK, S1.2, R3.Pin_0
  N2: Part1.A2_I34, R1.pin_1, R2.Pin_0
  N3: Part1.GND, R2.Pin_1, R3.Pin_1
  N4: Part1.3.3V, R1.pin_0, R4.Pin_0
  N5: S1.3, R4.Pin_1
