# Fritzing sketch esp32And522RFID (saved by Fritzing 0.9.4)
breadboards: 1

parts:
  Part1 = RFID-RC522-v2
  Part2 = Adafruit HUZZAH32 ESP32 Feather [part_number="Adafruit #3405"]

nets:
  N1: Part1.SDA, Part2.SDA
  N2: Part1.SCK, Part2.SCK
  N3: Part1.MOSI, Part2.MOSI
  N4: Part1.MISO, Part2.MISO
  GND: Part1.GND, Part2.GND
  N5: Part1.RST, Part2.IO21
  3.3V: Part1.3.3V, Part2.3.3V

custom parts:
  RFID-RC522-v2: A simple China made RFID-RC522 Reader; do check the pin labels, as this is a MFRC522 based clone.
