# Fritzing sketch esp32-button (saved by Fritzing 0.9.4)
breadboards: 1

parts:
  Part1 = Adafruit HUZZAH32 ESP32 Feather [part_number="Adafruit #3405"]
  S1 = Momentary Switch [package=ksa_sealed_tac_switch]
  R3 = Resistor [tolerance=±5% resistance=10k package="0805 [SMD]"]
  R4 = Resistor [tolerance=±5% resistance=1k package="0805 [SMD]"]

nets:
  N1: Part1.SCK, S1.2, R3.Pin_0
  N2: Part1.GND, R3.Pin_1
  N3: Part1.3.3V, R4.Pin_0
  N4: S1.3, R4.Pin_1
