# Fritzing sketch esp32And522RFID (saved by Fritzing 0.9.4)
breadboards: 1

parts:
  Part1 = RFID-RC522-v2
  Part2 = Adafruit HUZZAH32 ESP32 Feather [part_number="Adafruit #3405"]

nets:
  GND: Part1.GND, Part2.GND
  3.3V: Part1.3.3V, Part2.3.3V

custom parts:
  RFID-RC522-v2: A simple China made RFID-RC522 Reader; do check the pin labels, as this is a MFRC522 based clone.
