# Fritzing sketch unoAnd522RFID (saved by Fritzing 0.9.4)

parts:
  Part1 = RFID-RC522-v2
  Part2 = Arduino Uno (Rev3)

nets:
  N1: Part1.SDA, Part2.D10_PWM/SS
  N2: Part1.SCK, Part2.D13/SCK
  N3: Part1.MOSI, Part2.D11_PWM/MOSI
  N4: Part1.MISO, Part2.D12/MISO
  GND: Part1.GND, Part2.GND
  N5: Part1.RST, Part2.D9_PWM
  3.3V: Part1.3.3V, Part2.3V3

custom parts:
  RFID-RC522-v2: A simple China made RFID-RC522 Reader; do check the pin labels, as this is a MFRC522 based clone.
