# Fritzing sketch esp32-oledAndButton (saved by Fritzing 0.9.4)
breadboards: 1

parts:
  Part1 = Adafruit HUZZAH32 ESP32 Feather [part_number="Adafruit #3405"]
  Grove1 = Grove OLED 128x96
  R7 = Resistor [tolerance=±5% resistance=10k package=THT]
  R8 = Resistor [tolerance=±5% resistance=10k package=THT]
  R9 = Resistor [tolerance=±5% resistance=1k package="0805 [SMD]"]
  S2 = Momentary Switch [package=ksa_sealed_tac_switch]
  R10 = Resistor [tolerance=±5% resistance=10k package="0805 [SMD]"]

nets:
  N1: Part1.SCK, S2.2, R10.Pin_0
  GND: Part1.GND, Grove1.GND, R10.Pin_1
  3.3V: Part1.3.3V, Grove1.VCC, R7.Pin_0, R8.Pin_0, R9.Pin_0
  N2: Part1.SCL, Grove1.SDA, R8.Pin_1
  N3: Part1.SDA, Grove1.SCL, R7.Pin_1
  N4: R9.Pin_1, S2.3
