# Fritzing sketch SOUND-simple (saved by Fritzing 0.9.4)
breadboards: 1

parts:
  Part1 = Adafruit HUZZAH32 ESP32 Feather [part_number="Adafruit #3405"]
  C3 = Capacitor Polarized [package=cpol-radial-10uf-25v]
  SP1 = SPEAKER [package=pcb_mount_speaker]

nets:
  N1: Part1.A0_DAC2, C3.+
  N2: Part1.GND, SP1.-
  N3: C3.-, SP1.+
